// Digital circuit FormatDecoder.dig as structural Verilog
module FormatDecoder (
  input  [31:0] inst,
  input  [2:0] fmt,
  output [31:0] R,
  output [31:0] I,
  output [31:0] S,
  output [31:0] B,
  output [31:0] U,
  output [31:0] J
);

  Demultiplexer #(.Bits(32), .Selector_Bits(3)) demultiplexer_1 (
    .sel(fmt), .in(inst), .out_0(R), .out_1(I), .out_2(S), .out_3(B), .out_4(U), .out_5(J));  // open: out_6, out_7
endmodule
