// Digital circuit alu.dig as structural Verilog
module alu (
  input  [31:0] op1,
  input  [31:0] op2,
  input  [9:0] funct,
  output [31:0] result
);

  wire [1:0] funct7_decoder_1_funct_type;
  wire [2:0] demultiplexer_1_out_1;
  wire [31:0] add_1_s;

  funct7_decoder funct7_decoder_1 (.funct7(funct[9:3]), .funct_type(funct7_decoder_1_funct_type));
  Add #(.Bits(32)) add_1 (.a(op1), .b(op2), .c_i(1'b0), .s(add_1_s));  // open: c_o
  Demultiplexer #(.Selector_Bits(2), .Bits(3)) demultiplexer_1 (
    .sel(funct7_decoder_1_funct_type), .in(funct[2:0]), .out_1(demultiplexer_1_out_1));  // open: out_0, out_2, out_3
  Multiplexer #(.Selector_Bits(3), .Bits(32)) multiplexer_1 (
    .sel(demultiplexer_1_out_1), .in_0(add_1_s), .in_1({32{1'b0}}), .in_2({32{1'b0}}), .in_3({32{1'b0}}),
    .in_4({32{1'b0}}), .in_5({32{1'b0}}), .in_6({32{1'b0}}), .in_7({32{1'b0}}), .out(result));

  // Other names for the same wires on the sheet: funct3[2:0] = funct[2:0]; funct7[6:0] = funct[9:3]
endmodule
