// Digital circuit asm32.dig as structural Verilog
module asm32 (
  input  mode,
  input  [4:0] rd,
  input  [4:0] rs1,
  input  [4:0] rs2,
  input  [11:0] imm,
  input  add,
  input  jump,
  input  Rr,
  output store_clk,
  output [31:0] inst
);

  wire priorityencoder_1_any;
  wire [3:0] multiplexer_2_out;

  Multiplexer #(.Bits(12)) multiplexer_1 (.sel(Rr), .in_0(imm), .in_1({{7{1'b0}}, rs2}), .out(inst[31:20]));
  Multiplexer #(.Bits(4)) multiplexer_2 (.sel(Rr), .in_0(4'b0010), .in_1(4'b0001), .out(multiplexer_2_out));
  opcodes opcodes_1 (.addr(multiplexer_2_out), .D_out(inst[6:0]));
  PriorityEncoder #(.Selector_Bits(3)) priorityencoder_1 (
    .in0(add), .in1(1'b0), .in2(1'b0), .in3(1'b0), .in4(1'b0), .in5(1'b0), .in6(1'b0), .in7(jump),
    .num(inst[14:12]), .any(priorityencoder_1_any));
  and and_1 (store_clk, priorityencoder_1_any, mode);

  assign {inst[19:15], inst[11:7]} = {rs1, rd};

  // Notes on the sheet:
  //   mode: default 1
  //   rd: default 1
  //   rs1: default 1
  //   rs2: default 4
  //   imm: default 1
  //   add: default 100
endmodule
