// Digital circuit componenttest.dig as structural Verilog
module componenttest (
  input  [4:0] rs1,
  input  [4:0] rs2,
  input  [4:0] rd,
  input  [31:0] data,
  input  clock,
  output [31:0] out_rs1,
  output [31:0] out_rs2
);

  register_file register_file_1 (
    .rs1(rs1), .rs2(rs2), .rd(rd), .D_in(data), .clock(clock), .D_rs1(out_rs1), .D_rs2(out_rs2));
endmodule
