// Digital circuit dec2.dig as structural Verilog
module dec2 (
  input  [6:0] opcode,
  input  [31:0] instr,
  input  [31:0] val_rs1,
  input  [31:0] val_rs2,
  output [4:0] rs1,
  output [4:0] rs2,
  output [4:0] rd,
  output [31:0] op1,
  output [31:0] op2,
  output [9:0] funct
);

  wire [2:0] rom_1_d;
  wire [31:0] demultiplexer_1_out_1, demultiplexer_1_out_2;

  ROM #(.AddrBits(5), .Bits(3)) rom_1 (.A(opcode[6:2]), .sel(1'b1), .D(rom_1_d));
  Demultiplexer #(.Selector_Bits(3), .Bits(32)) demultiplexer_1 (
    .sel(rom_1_d), .in(instr), .out_1(demultiplexer_1_out_1), .out_2(demultiplexer_1_out_2));  // open: out_0, out_3, out_4, out_5, out_6, out_7
  r_type_decoder r_type_decoder_1 (
    .instr(demultiplexer_1_out_1), .val_rs1(val_rs1), .val_rs2(val_rs2), .rd(rd), .rs1(rs1), .rs2(rs2),
    .op1(op1), .op2(op2), .funct(funct));
  i_type_decoder i_type_decoder_1 (
    .instr(demultiplexer_1_out_2), .val_rs1(val_rs1), .rd(rd), .rs1(rs1), .op1(op1), .op2(op2), .funct(funct));

  // Other names for the same wires on the sheet: v_rs1[31:0] = val_rs1; v_rs2[31:0] = val_rs2

  // Notes on the sheet:
  //   contents of rom_1 (hex, n*v repeats v):
  //   2,0,0,0,2,5,0,0,3,0,0,0,1,5,10*0,4,2,0,6,2
endmodule
