// Digital circuit decoder.dig as structural Verilog
module decoder (
  input  [31:0] D_inst,
  input  [31:0] Val_rs1,
  input  [31:0] Val_rs2,
  output [4:0] rs_1,
  output [4:0] rs_2,
  output [4:0] rd,
  output [31:0] Op_1,
  output [31:0] Op_2,
  output add,
  output jump
);

  wire and_1_out, demultiplexer_1_out_4, demultiplexer_2_out_0;

  and and_1 (and_1_out, demultiplexer_1_out_4, demultiplexer_2_out_0);
  Multiplexer #(.Bits(32)) multiplexer_1 (
    .sel(and_1_out), .in_0(Val_rs2), .in_1({{20{1'b0}}, D_inst[31:20]}), .out(Op_1));
  Demultiplexer #(.Selector_Bits(3)) demultiplexer_1 (
    .sel(D_inst[4:2]), .in(1'b1), .out_4(demultiplexer_1_out_4));  // open: out_0, out_1, out_2, out_3, out_5, out_6, out_7
  Demultiplexer #(.Selector_Bits(2)) demultiplexer_2 (
    .sel(D_inst[6:5]), .in(1'b1), .out_0(demultiplexer_2_out_0));  // open: out_1, out_2, out_3
  Decoder #(.Selector_Bits(3)) decoder_1 (
    .sel(D_inst[14:12]), .out_0(add), .out_7(jump));  // open: out_1, out_2, out_3, out_4, out_5, out_6

  assign Op_2 = Val_rs1;
  assign rd = D_inst[11:7];
  assign rs_1 = D_inst[19:15];
  assign rs_2 = D_inst[24:20];

  // Notes on the sheet:
  //   D_inst: Take 32-bits input
  //   Val_rs1: Value from rs1 register
  //   Val_rs2: Value from rs2 register
  //   Op_1: Operand 1
  //   Op_2: Operand 2
endmodule
