// Digital circuit execute.dig as structural Verilog
module execute (
  input  [31:0] Op_1,
  input  [31:0] Op_2,
  input  add,
  output [31:0] result
);

  wire [31:0] add_1_s;

  Add #(.Bits(32)) add_1 (.a(Op_1), .b(Op_2), .c_i(1'b0), .s(add_1_s));  // open: c_o
  Multiplexer #(.Bits(32)) multiplexer_1 (.sel(add), .in_0(Op_2), .in_1(add_1_s), .out(result));

  // Notes on the sheet:
  //   Op_1: Operand 1
  //   Op_2: Operand 2
endmodule
