// Digital circuit funct7_decoder.dig as structural Verilog
module funct7_decoder (
  input  [6:0] funct7,
  output [1:0] funct_type
);

  wire comparator_1_eq, comparator_2_eq, comparator_3_eq, comparator_4_eq;

  Comparator #(.Bits(7)) comparator_1 (.a(funct7), .b({7{1'b0}}), .eq(comparator_1_eq));  // open: gt, lt
  Comparator #(.Bits(7)) comparator_2 (.a(funct7), .b(7'b0000001), .eq(comparator_2_eq));  // open: gt, lt
  Comparator #(.Bits(7)) comparator_3 (.a(funct7), .b(7'b0010000), .eq(comparator_3_eq));  // open: gt, lt
  Comparator #(.Bits(7)) comparator_4 (.a(funct7), .b(7'b0100000), .eq(comparator_4_eq));  // open: gt, lt
  PriorityEncoder #(.Selector_Bits(2)) priorityencoder_1 (
    .in0(comparator_1_eq), .in1(comparator_2_eq), .in2(comparator_3_eq), .in3(comparator_4_eq),
    .num(funct_type));  // open: any
endmodule
