// Digital circuit i_type_decoder.dig as structural Verilog
module i_type_decoder (
  input  [31:0] instr,
  input  [31:0] val_rs1,
  output [4:0] rd,
  output [4:0] rs1,
  output [31:0] op1,
  output [31:0] op2,
  output [9:0] funct
);

  BitExtender #(.inputBits(12), .outputBits(32)) bitextender_1 (.in(instr[31:20]), .out(op2));

  assign funct = {{7{1'b0}}, instr[14:12]};
  assign op1 = val_rs1;
  assign rd = instr[11:7];
  assign rs1 = instr[19:15];

  // Notes on the sheet:
  //   op1: Operand 1
  //   funct: The function to apply
endmodule
