// Digital circuit opcodes.dig as structural Verilog
module opcodes (
  input  [3:0] addr,
  output [6:0] D_out
);

  ROM #(.AddrBits(4), .Bits(7)) rom_1 (.A(addr), .sel(1'b1), .D(D_out));

  // Notes on the sheet:
  //   contents of rom_1 (hex, n*v repeats v):
  //   0,33,13,3,23,63,6f,67,37,17,73
endmodule
