// Digital circuit r_type_decoder.dig as structural Verilog
module r_type_decoder (
  input  [31:0] instr,
  input  [31:0] val_rs1,
  input  [31:0] val_rs2,
  output [4:0] rd,
  output [4:0] rs1,
  output [4:0] rs2,
  output [31:0] op1,
  output [31:0] op2,
  output [9:0] funct
);


  assign funct = {instr[31:25], instr[14:12]};
  assign op1 = val_rs1;
  assign op2 = val_rs2;
  assign rd = instr[11:7];
  assign rs1 = instr[19:15];
  assign rs2 = instr[24:20];

  // Notes on the sheet:
  //   op1: Operand 1
  //   op2: Operand 2
  //   funct: The function to perform on operands
endmodule
