// Digital circuit register_file.dig as structural Verilog
// Register file with 32 32-bit registers
module register_file (
  input  [4:0] rs1,
  input  [4:0] rs2,
  input  [4:0] rd,
  input  [31:0] D_in,
  input  clock,
  output [31:0] D_rs1,
  output [31:0] D_rs2
);

  wire demultiplexer_2_out_16, demultiplexer_2_out_17, demultiplexer_2_out_18, demultiplexer_2_out_19,
       demultiplexer_2_out_20, demultiplexer_2_out_21, demultiplexer_2_out_22, demultiplexer_2_out_23,
       demultiplexer_2_out_24, demultiplexer_2_out_25, demultiplexer_2_out_26, demultiplexer_2_out_27,
       demultiplexer_2_out_28, demultiplexer_2_out_29, demultiplexer_2_out_30, demultiplexer_2_out_31,
       register_1_p3, register_2_p3, register_3_p3, register_4_p3, register_5_p3, register_6_p3,
       register_7_p3, register_8_p3, register_9_p3, register_10_p3, register_11_p3, register_12_p3,
       register_13_p3, register_14_p3, register_15_p3, register_16_p3;
  wire [31:0] demultiplexer_1_out_0, demultiplexer_1_out_16, demultiplexer_1_out_17, demultiplexer_1_out_18,
       demultiplexer_1_out_19, demultiplexer_1_out_20, demultiplexer_1_out_21, demultiplexer_1_out_22,
       demultiplexer_1_out_23, demultiplexer_1_out_24, demultiplexer_1_out_25, demultiplexer_1_out_26,
       demultiplexer_1_out_27, demultiplexer_1_out_28, demultiplexer_1_out_29, demultiplexer_1_out_30,
       demultiplexer_1_out_31, nor_1_out, register_1_p4, register_2_p1, register_2_p4, register_3_p1,
       register_3_p4, register_4_p1, register_4_p4, register_5_p1, register_5_p4, register_6_p1,
       register_6_p4, register_7_p1, register_7_p4, register_8_p1, register_8_p4, register_9_p1,
       register_9_p4, register_10_p1, register_10_p4, register_11_p1, register_11_p4, register_12_p1,
       register_12_p4, register_13_p1, register_13_p4, register_14_p1, register_14_p4, register_15_p1,
       register_15_p4, register_16_p1, register_16_p4, register_17_p1, register_18_p1, register_19_p1,
       register_20_p1, register_21_p1, register_22_p1, register_23_p1, register_24_p1, register_25_p1,
       register_26_p1, register_27_p1, register_28_p1, register_29_p1, register_30_p1, register_31_p1,
       register_32_p1;

  assign nor_1_out = ~({32{1'b1}} | demultiplexer_1_out_0);  // NOr nor_1, 32 bits wide
  // register register_1: pin names not known; wires that end beside it: nor_1_out, clock, register_1_p3, register_1_p4
  // register register_2: pin names not known; wires that end beside it: register_2_p1, clock, register_2_p3, register_2_p4
  // register register_3: pin names not known; wires that end beside it: register_3_p1, clock, register_3_p3, register_3_p4
  // register register_4: pin names not known; wires that end beside it: register_4_p1, clock, register_4_p3, register_4_p4
  // register register_5: pin names not known; wires that end beside it: register_5_p1, clock, register_5_p3, register_5_p4
  // register register_6: pin names not known; wires that end beside it: register_6_p1, clock, register_6_p3, register_6_p4
  // register register_7: pin names not known; wires that end beside it: register_7_p1, clock, register_7_p3, register_7_p4
  // register register_8: pin names not known; wires that end beside it: register_8_p1, clock, register_8_p3, register_8_p4
  // register register_9: pin names not known; wires that end beside it: register_9_p1, clock, register_9_p3, register_9_p4
  // register register_10: pin names not known; wires that end beside it: register_10_p1, clock, register_10_p3, register_10_p4
  // register register_11: pin names not known; wires that end beside it: register_11_p1, clock, register_11_p3, register_11_p4
  // register register_12: pin names not known; wires that end beside it: register_12_p1, clock, register_12_p3, register_12_p4
  // register register_13: pin names not known; wires that end beside it: register_13_p1, clock, register_13_p3, register_13_p4
  // register register_14: pin names not known; wires that end beside it: register_14_p1, clock, register_14_p3, register_14_p4
  // register register_15: pin names not known; wires that end beside it: register_15_p1, clock, register_15_p3, register_15_p4
  // register register_16: pin names not known; wires that end beside it: register_16_p1, clock, register_16_p3, register_16_p4
  Multiplexer #(.Selector_Bits(5), .Bits(32)) multiplexer_1 (
    .sel(rs1), .in_0(register_1_p4), .in_1(register_2_p4), .in_2(register_3_p4), .in_3(register_4_p4),
    .in_4(register_5_p4), .in_5(register_6_p4), .in_6(register_7_p4), .in_7(register_8_p4),
    .in_8(register_9_p4), .in_9(register_10_p4), .in_10(register_11_p4), .in_11(register_12_p4),
    .in_12(register_13_p4), .in_13(register_14_p4), .in_14(register_15_p4), .in_15(register_16_p4),
    .in_16(register_24_p1), .in_17(register_23_p1), .in_18(register_22_p1), .in_19(register_21_p1),
    .in_20(register_20_p1), .in_21(register_19_p1), .in_22(register_18_p1), .in_23(register_17_p1),
    .in_24(register_32_p1), .in_25(register_31_p1), .in_26(register_30_p1), .in_27(register_29_p1),
    .in_28(register_28_p1), .in_29(register_27_p1), .in_30(register_26_p1), .in_31(register_25_p1),
    .out(D_rs1));
  Demultiplexer #(.Selector_Bits(5), .Bits(32)) demultiplexer_1 (
    .sel(rd), .in(D_in), .out_0(demultiplexer_1_out_0), .out_1(register_2_p1), .out_2(register_3_p1),
    .out_3(register_4_p1), .out_4(register_5_p1), .out_5(register_6_p1), .out_6(register_7_p1),
    .out_7(register_8_p1), .out_8(register_9_p1), .out_9(register_10_p1), .out_10(register_11_p1),
    .out_11(register_12_p1), .out_12(register_13_p1), .out_13(register_14_p1), .out_14(register_15_p1),
    .out_15(register_16_p1), .out_16(demultiplexer_1_out_16), .out_17(demultiplexer_1_out_17),
    .out_18(demultiplexer_1_out_18), .out_19(demultiplexer_1_out_19), .out_20(demultiplexer_1_out_20),
    .out_21(demultiplexer_1_out_21), .out_22(demultiplexer_1_out_22), .out_23(demultiplexer_1_out_23),
    .out_24(demultiplexer_1_out_24), .out_25(demultiplexer_1_out_25), .out_26(demultiplexer_1_out_26),
    .out_27(demultiplexer_1_out_27), .out_28(demultiplexer_1_out_28), .out_29(demultiplexer_1_out_29),
    .out_30(demultiplexer_1_out_30), .out_31(demultiplexer_1_out_31));
  Demultiplexer #(.Selector_Bits(5)) demultiplexer_2 (
    .sel(rd), .in(1'b1), .out_0(register_1_p3), .out_1(register_2_p3), .out_2(register_3_p3),
    .out_3(register_4_p3), .out_4(register_5_p3), .out_5(register_6_p3), .out_6(register_7_p3),
    .out_7(register_8_p3), .out_8(register_9_p3), .out_9(register_10_p3), .out_10(register_11_p3),
    .out_11(register_12_p3), .out_12(register_13_p3), .out_13(register_14_p3), .out_14(register_15_p3),
    .out_15(register_16_p3), .out_16(demultiplexer_2_out_16), .out_17(demultiplexer_2_out_17),
    .out_18(demultiplexer_2_out_18), .out_19(demultiplexer_2_out_19), .out_20(demultiplexer_2_out_20),
    .out_21(demultiplexer_2_out_21), .out_22(demultiplexer_2_out_22), .out_23(demultiplexer_2_out_23),
    .out_24(demultiplexer_2_out_24), .out_25(demultiplexer_2_out_25), .out_26(demultiplexer_2_out_26),
    .out_27(demultiplexer_2_out_27), .out_28(demultiplexer_2_out_28), .out_29(demultiplexer_2_out_29),
    .out_30(demultiplexer_2_out_30), .out_31(demultiplexer_2_out_31));
  Multiplexer #(.Selector_Bits(5), .Bits(32)) multiplexer_2 (
    .sel(rs2), .in_0(register_1_p4), .in_1(register_2_p4), .in_2(register_3_p4), .in_3(register_4_p4),
    .in_4(register_5_p4), .in_5(register_6_p4), .in_6(register_7_p4), .in_7(register_8_p4),
    .in_8(register_9_p4), .in_9(register_10_p4), .in_10(register_11_p4), .in_11(register_12_p4),
    .in_12(register_13_p4), .in_13(register_14_p4), .in_14(register_15_p4), .in_15(register_16_p4),
    .in_16(register_24_p1), .in_17(register_23_p1), .in_18(register_22_p1), .in_19(register_21_p1),
    .in_20(register_20_p1), .in_21(register_19_p1), .in_22(register_18_p1), .in_23(register_17_p1),
    .in_24(register_32_p1), .in_25(register_31_p1), .in_26(register_30_p1), .in_27(register_29_p1),
    .in_28(register_28_p1), .in_29(register_27_p1), .in_30(register_26_p1), .in_31(register_25_p1),
    .out(D_rs2));
  // register register_17: pin names not known; wires that end beside it: register_17_p1, demultiplexer_2_out_23, clock, demultiplexer_1_out_23
  // register register_18: pin names not known; wires that end beside it: register_18_p1, demultiplexer_2_out_22, clock, demultiplexer_1_out_22
  // register register_19: pin names not known; wires that end beside it: register_19_p1, demultiplexer_2_out_21, clock, demultiplexer_1_out_21
  // register register_20: pin names not known; wires that end beside it: register_20_p1, demultiplexer_2_out_20, clock, demultiplexer_1_out_20
  // register register_21: pin names not known; wires that end beside it: register_21_p1, demultiplexer_2_out_19, clock, demultiplexer_1_out_19
  // register register_22: pin names not known; wires that end beside it: register_22_p1, demultiplexer_2_out_18, clock, demultiplexer_1_out_18
  // register register_23: pin names not known; wires that end beside it: register_23_p1, demultiplexer_2_out_17, clock, demultiplexer_1_out_17
  // register register_24: pin names not known; wires that end beside it: register_24_p1, demultiplexer_2_out_16, clock, demultiplexer_1_out_16
  // register register_25: pin names not known; wires that end beside it: register_25_p1, demultiplexer_2_out_31, clock, demultiplexer_1_out_31
  // register register_26: pin names not known; wires that end beside it: register_26_p1, demultiplexer_2_out_30, clock, demultiplexer_1_out_30
  // register register_27: pin names not known; wires that end beside it: register_27_p1, demultiplexer_2_out_29, clock, demultiplexer_1_out_29
  // register register_28: pin names not known; wires that end beside it: register_28_p1, demultiplexer_2_out_28, clock, demultiplexer_1_out_28
  // register register_29: pin names not known; wires that end beside it: register_29_p1, demultiplexer_2_out_27, clock, demultiplexer_1_out_27
  // register register_30: pin names not known; wires that end beside it: register_30_p1, demultiplexer_2_out_26, clock, demultiplexer_1_out_26
  // register register_31: pin names not known; wires that end beside it: register_31_p1, demultiplexer_2_out_25, clock, demultiplexer_1_out_25
  // register register_32: pin names not known; wires that end beside it: register_32_p1, demultiplexer_2_out_24, clock, demultiplexer_1_out_24

  // Notes on the sheet:
  //   D_rs1: This outputs the 32-bit data stored at the register specified by rs1
  //   D_rs2: This outputs the 32-bit data stored at the register specified by rs2
  //   D_in: 32-bit input to be stored at rd
endmodule

/* Test case Register IO:
		clock	rd	D_in 		rs1	D_rs1		rs2	D_rs2
		C	0	0x77 		0	0		0	0
repeat(31)	C     	(n+1) 	(0x7<<n) 	(n+1)	(0x7<<n) 	(n+1)	(0x7<<n)
*/
