// Digital circuit s_type_decoder.dig as structural Verilog
module s_type_decoder (
  input  [31:0] instr,
  output [4:0] imm5,
  output [4:0] rs1,
  output [4:0] rs2,
  output [6:0] imm7
);


  assign imm5 = instr[11:7];
  assign imm7 = instr[31:25];
  assign rs1 = instr[19:15];
  assign rs2 = instr[24:20];
endmodule
