// Digital circuit soc.dig as structural Verilog
module soc (
  input  [4:0] dest,
  input  [4:0] src1,
  input  R_R,
  input  [11:0] value,
  input  [4:0] src2,
  output [4:0] rs,
  output [31:0] L,
  output [31:0] R,
  output [4:0] rd,
  output [3:0] pc,
  output [31:0] L_2,
  output [31:0] L_rs,
  output [31:0] R_rd,
  output [31:0] out_12
);

  wire add, add_out, advance_out, asm32_1_store_clk, jmp, jmp_out, mode_out, pmshim32_1_p6, pmshim32_1_p7,
       pmshim32_1_p8;
  wire [3:0] pmshim32_1_p4;
  wire [4:0] decoder_1_rs_2;
  wire [31:0] asm32_1_inst, fetch_1_d_inst, pmshim32_1_p5, Program_d;

  LED programming (.in(mode_out));
  DipSwitch mode (.out(mode_out));
  Button u_add (.out(add_out));
  Button u_jmp (.out(jmp_out));
  asm32 asm32_1 (
    .mode(mode_out), .rd(dest), .rs1(src1), .rs2(src2), .imm(value), .add(add_out), .jump(jmp_out), .Rr(R_R),
    .store_clk(asm32_1_store_clk), .inst(asm32_1_inst));
  // pmshim32 pmshim32_1: pin names not known; wires that end beside it: pc, asm32_1_store_clk, asm32_1_inst, pmshim32_1_p4, pmshim32_1_p5, pmshim32_1_p6, pmshim32_1_p7, pmshim32_1_p8
  EEPROMDualPort #(.AddrBits(4), .Bits(32)) Program (
    .A(pmshim32_1_p4), .Din(pmshim32_1_p5), .str(pmshim32_1_p6), .C(pmshim32_1_p7), .ld(pmshim32_1_p8),
    .D(Program_d));
  Button advance (.out(advance_out));
  fetch fetch_1 (
    .mode(mode_out), .D_stored(Program_d), .D_bypass(asm32_1_inst), .C(advance_out), .value(L), .jump(jmp),
    .pc(pc), .D_inst(fetch_1_d_inst));
  LED add_2 (.in(add));
  LED jump (.in(jmp));
  decoder decoder_1 (
    .D_inst(fetch_1_d_inst), .Val_rs1(L_rs), .Val_rs2(R_rd), .rs_1(rs), .rs_2(decoder_1_rs_2), .rd(rd),
    .Op_1(L), .Op_2(R), .add(add), .jump(jmp));
  execute execute_1 (.Op_1(L), .Op_2(R), .add(add), .result(out_12));
  register_file register_file_1 (
    .rs1(rs), .rs2(decoder_1_rs_2), .rd(rd), .D_in(out_12), .clock(advance_out), .D_rs1(L_rs), .D_rs2(R_rd));

  assign L_2 = L;
endmodule
