// Digital circuit u_type_decoder.dig as structural Verilog
module u_type_decoder (
  input  [31:0] instr,
  output [4:0] rd,
  output [19:0] imm20
);

  // Pins of 7 and 20 bits meet at instr[31:12]

  assign imm20 = instr[31:12];
  assign rd = instr[11:7];
endmodule
