// Digital circuit Register.dig as structural Verilog
module Register (
  input  [4:0] rd,
  input  [31:0] W,
  input  C,
  input  [4:0] rs1,
  input  [4:0] rs2,
  output [31:0] R2,
  output [31:0] R1
);

  wire demultiplexer_2_out_0, demultiplexer_2_out_1, demultiplexer_2_out_2, demultiplexer_2_out_3,
       demultiplexer_2_out_4, demultiplexer_2_out_5, demultiplexer_2_out_6, demultiplexer_2_out_7,
       demultiplexer_2_out_8, demultiplexer_2_out_9, demultiplexer_2_out_10, demultiplexer_2_out_11,
       demultiplexer_2_out_12, demultiplexer_2_out_13, demultiplexer_2_out_14, demultiplexer_2_out_15,
       demultiplexer_2_out_16, demultiplexer_2_out_17, demultiplexer_2_out_18, demultiplexer_2_out_19,
       demultiplexer_2_out_20, demultiplexer_2_out_21, demultiplexer_2_out_22, demultiplexer_2_out_23,
       demultiplexer_2_out_24, demultiplexer_2_out_25, demultiplexer_2_out_26, demultiplexer_2_out_27,
       demultiplexer_2_out_28, demultiplexer_2_out_29, demultiplexer_2_out_30, demultiplexer_2_out_31;
  wire [31:0] demultiplexer_1_out_0, demultiplexer_1_out_1, demultiplexer_1_out_2, demultiplexer_1_out_3,
       demultiplexer_1_out_4, demultiplexer_1_out_5, demultiplexer_1_out_6, demultiplexer_1_out_7,
       demultiplexer_1_out_8, demultiplexer_1_out_9, demultiplexer_1_out_10, demultiplexer_1_out_11,
       demultiplexer_1_out_12, demultiplexer_1_out_13, demultiplexer_1_out_14, demultiplexer_1_out_15,
       demultiplexer_1_out_16, demultiplexer_1_out_17, demultiplexer_1_out_18, demultiplexer_1_out_19,
       demultiplexer_1_out_20, demultiplexer_1_out_21, demultiplexer_1_out_22, demultiplexer_1_out_23,
       demultiplexer_1_out_24, demultiplexer_1_out_25, demultiplexer_1_out_26, demultiplexer_1_out_27,
       demultiplexer_1_out_28, demultiplexer_1_out_29, demultiplexer_1_out_30, demultiplexer_1_out_31,
       nor_1_out, reg_1_q, reg_2_q, reg_3_q, reg_4_q, reg_5_q, reg_6_q, reg_7_q, reg_8_q, reg_9_q, reg_10_q,
       reg_11_q, reg_12_q, reg_13_q, reg_14_q, reg_15_q, reg_16_q, reg_17_q, reg_18_q, reg_19_q, reg_20_q,
       reg_21_q, reg_22_q, reg_23_q, reg_24_q, reg_25_q, reg_26_q, reg_27_q, reg_28_q, reg_29_q, reg_30_q,
       reg_31_q, reg_32_q;

  assign nor_1_out = ~({32{1'b1}} | demultiplexer_1_out_0);  // NOr nor_1, 32 bits wide
  \reg  reg_1 (.D(nor_1_out), .C(C), .en(demultiplexer_2_out_0), .Q(reg_1_q));
  \reg  reg_2 (.D(demultiplexer_1_out_1), .C(C), .en(demultiplexer_2_out_1), .Q(reg_2_q));
  \reg  reg_3 (.D(demultiplexer_1_out_2), .C(C), .en(demultiplexer_2_out_2), .Q(reg_3_q));
  \reg  reg_4 (.D(demultiplexer_1_out_3), .C(C), .en(demultiplexer_2_out_3), .Q(reg_4_q));
  \reg  reg_5 (.D(demultiplexer_1_out_4), .C(C), .en(demultiplexer_2_out_4), .Q(reg_5_q));
  \reg  reg_6 (.D(demultiplexer_1_out_5), .C(C), .en(demultiplexer_2_out_5), .Q(reg_6_q));
  \reg  reg_7 (.D(demultiplexer_1_out_6), .C(C), .en(demultiplexer_2_out_6), .Q(reg_7_q));
  \reg  reg_8 (.D(demultiplexer_1_out_7), .C(C), .en(demultiplexer_2_out_7), .Q(reg_8_q));
  \reg  reg_9 (.D(demultiplexer_1_out_8), .C(C), .en(demultiplexer_2_out_8), .Q(reg_9_q));
  \reg  reg_10 (.D(demultiplexer_1_out_9), .C(C), .en(demultiplexer_2_out_9), .Q(reg_10_q));
  \reg  reg_11 (.D(demultiplexer_1_out_10), .C(C), .en(demultiplexer_2_out_10), .Q(reg_11_q));
  \reg  reg_12 (.D(demultiplexer_1_out_11), .C(C), .en(demultiplexer_2_out_11), .Q(reg_12_q));
  \reg  reg_13 (.D(demultiplexer_1_out_12), .C(C), .en(demultiplexer_2_out_12), .Q(reg_13_q));
  \reg  reg_14 (.D(demultiplexer_1_out_13), .C(C), .en(demultiplexer_2_out_13), .Q(reg_14_q));
  \reg  reg_15 (.D(demultiplexer_1_out_14), .C(C), .en(demultiplexer_2_out_14), .Q(reg_15_q));
  \reg  reg_16 (.D(demultiplexer_1_out_15), .C(C), .en(demultiplexer_2_out_15), .Q(reg_16_q));
  Multiplexer #(.Selector_Bits(5), .Bits(32)) multiplexer_1 (
    .sel(rs1), .in_0(reg_1_q), .in_1(reg_2_q), .in_2(reg_3_q), .in_3(reg_4_q), .in_4(reg_5_q),
    .in_5(reg_6_q), .in_6(reg_7_q), .in_7(reg_8_q), .in_8(reg_9_q), .in_9(reg_10_q), .in_10(reg_11_q),
    .in_11(reg_12_q), .in_12(reg_13_q), .in_13(reg_14_q), .in_14(reg_15_q), .in_15(reg_16_q),
    .in_16(reg_24_q), .in_17(reg_23_q), .in_18(reg_22_q), .in_19(reg_21_q), .in_20(reg_20_q),
    .in_21(reg_19_q), .in_22(reg_18_q), .in_23(reg_17_q), .in_24(reg_32_q), .in_25(reg_31_q),
    .in_26(reg_30_q), .in_27(reg_29_q), .in_28(reg_28_q), .in_29(reg_27_q), .in_30(reg_26_q),
    .in_31(reg_25_q), .out(R1));
  Demultiplexer #(.Bits(32), .Selector_Bits(5)) demultiplexer_1 (
    .sel(rd), .in(W), .out_0(demultiplexer_1_out_0), .out_1(demultiplexer_1_out_1),
    .out_2(demultiplexer_1_out_2), .out_3(demultiplexer_1_out_3), .out_4(demultiplexer_1_out_4),
    .out_5(demultiplexer_1_out_5), .out_6(demultiplexer_1_out_6), .out_7(demultiplexer_1_out_7),
    .out_8(demultiplexer_1_out_8), .out_9(demultiplexer_1_out_9), .out_10(demultiplexer_1_out_10),
    .out_11(demultiplexer_1_out_11), .out_12(demultiplexer_1_out_12), .out_13(demultiplexer_1_out_13),
    .out_14(demultiplexer_1_out_14), .out_15(demultiplexer_1_out_15), .out_16(demultiplexer_1_out_16),
    .out_17(demultiplexer_1_out_17), .out_18(demultiplexer_1_out_18), .out_19(demultiplexer_1_out_19),
    .out_20(demultiplexer_1_out_20), .out_21(demultiplexer_1_out_21), .out_22(demultiplexer_1_out_22),
    .out_23(demultiplexer_1_out_23), .out_24(demultiplexer_1_out_24), .out_25(demultiplexer_1_out_25),
    .out_26(demultiplexer_1_out_26), .out_27(demultiplexer_1_out_27), .out_28(demultiplexer_1_out_28),
    .out_29(demultiplexer_1_out_29), .out_30(demultiplexer_1_out_30), .out_31(demultiplexer_1_out_31));
  Demultiplexer #(.Selector_Bits(5)) demultiplexer_2 (
    .sel(rd), .in(1'b1), .out_0(demultiplexer_2_out_0), .out_1(demultiplexer_2_out_1),
    .out_2(demultiplexer_2_out_2), .out_3(demultiplexer_2_out_3), .out_4(demultiplexer_2_out_4),
    .out_5(demultiplexer_2_out_5), .out_6(demultiplexer_2_out_6), .out_7(demultiplexer_2_out_7),
    .out_8(demultiplexer_2_out_8), .out_9(demultiplexer_2_out_9), .out_10(demultiplexer_2_out_10),
    .out_11(demultiplexer_2_out_11), .out_12(demultiplexer_2_out_12), .out_13(demultiplexer_2_out_13),
    .out_14(demultiplexer_2_out_14), .out_15(demultiplexer_2_out_15), .out_16(demultiplexer_2_out_16),
    .out_17(demultiplexer_2_out_17), .out_18(demultiplexer_2_out_18), .out_19(demultiplexer_2_out_19),
    .out_20(demultiplexer_2_out_20), .out_21(demultiplexer_2_out_21), .out_22(demultiplexer_2_out_22),
    .out_23(demultiplexer_2_out_23), .out_24(demultiplexer_2_out_24), .out_25(demultiplexer_2_out_25),
    .out_26(demultiplexer_2_out_26), .out_27(demultiplexer_2_out_27), .out_28(demultiplexer_2_out_28),
    .out_29(demultiplexer_2_out_29), .out_30(demultiplexer_2_out_30), .out_31(demultiplexer_2_out_31));
  Multiplexer #(.Bits(32), .Selector_Bits(5)) multiplexer_2 (
    .sel(rs2), .in_0(reg_1_q), .in_1(reg_2_q), .in_2(reg_3_q), .in_3(reg_4_q), .in_4(reg_5_q),
    .in_5(reg_6_q), .in_6(reg_7_q), .in_7(reg_8_q), .in_8(reg_9_q), .in_9(reg_10_q), .in_10(reg_11_q),
    .in_11(reg_12_q), .in_12(reg_13_q), .in_13(reg_14_q), .in_14(reg_15_q), .in_15(reg_16_q),
    .in_16(reg_24_q), .in_17(reg_23_q), .in_18(reg_22_q), .in_19(reg_21_q), .in_20(reg_20_q),
    .in_21(reg_19_q), .in_22(reg_18_q), .in_23(reg_17_q), .in_24(reg_32_q), .in_25(reg_31_q),
    .in_26(reg_30_q), .in_27(reg_29_q), .in_28(reg_28_q), .in_29(reg_27_q), .in_30(reg_26_q),
    .in_31(reg_25_q), .out(R2));
  \reg  reg_17 (.D(demultiplexer_1_out_23), .C(C), .en(demultiplexer_2_out_23), .Q(reg_17_q));
  \reg  reg_18 (.D(demultiplexer_1_out_22), .C(C), .en(demultiplexer_2_out_22), .Q(reg_18_q));
  \reg  reg_19 (.D(demultiplexer_1_out_21), .C(C), .en(demultiplexer_2_out_21), .Q(reg_19_q));
  \reg  reg_20 (.D(demultiplexer_1_out_20), .C(C), .en(demultiplexer_2_out_20), .Q(reg_20_q));
  \reg  reg_21 (.D(demultiplexer_1_out_19), .C(C), .en(demultiplexer_2_out_19), .Q(reg_21_q));
  \reg  reg_22 (.D(demultiplexer_1_out_18), .C(C), .en(demultiplexer_2_out_18), .Q(reg_22_q));
  \reg  reg_23 (.D(demultiplexer_1_out_17), .C(C), .en(demultiplexer_2_out_17), .Q(reg_23_q));
  \reg  reg_24 (.D(demultiplexer_1_out_16), .C(C), .en(demultiplexer_2_out_16), .Q(reg_24_q));
  \reg  reg_25 (.D(demultiplexer_1_out_31), .C(C), .en(demultiplexer_2_out_31), .Q(reg_25_q));
  \reg  reg_26 (.D(demultiplexer_1_out_30), .C(C), .en(demultiplexer_2_out_30), .Q(reg_26_q));
  \reg  reg_27 (.D(demultiplexer_1_out_29), .C(C), .en(demultiplexer_2_out_29), .Q(reg_27_q));
  \reg  reg_28 (.D(demultiplexer_1_out_28), .C(C), .en(demultiplexer_2_out_28), .Q(reg_28_q));
  \reg  reg_29 (.D(demultiplexer_1_out_27), .C(C), .en(demultiplexer_2_out_27), .Q(reg_29_q));
  \reg  reg_30 (.D(demultiplexer_1_out_26), .C(C), .en(demultiplexer_2_out_26), .Q(reg_30_q));
  \reg  reg_31 (.D(demultiplexer_1_out_25), .C(C), .en(demultiplexer_2_out_25), .Q(reg_31_q));
  \reg  reg_32 (.D(demultiplexer_1_out_24), .C(C), .en(demultiplexer_2_out_24), .Q(reg_32_q));
endmodule
