// Digital circuit decoder.dig as structural Verilog
module decoder (
  input  [31:0] D,
  input  [15:0] L_in,
  input  [15:0] R_in,
  output [1:0] rs,
  output [1:0] rd,
  output [15:0] L_out,
  output [15:0] R_out,
  output add,
  output jump
);

  wire [15:0] multiplexer_2_out;

  Multiplexer #(.Bits(16)) multiplexer_1 (.sel(D[27]), .in_0(D[15:0]), .in_1(L_in), .out(L_out));
  Multiplexer #(.Bits(16)) multiplexer_2 (.sel(D[27]), .in_0(L_in), .in_1(R_in), .out(multiplexer_2_out));
  Decoder #(.Selector_Bits(3)) decoder_1 (
    .sel(D[26:24]), .out_0(add), .out_7(jump));  // open: out_1, out_2, out_3, out_4, out_5, out_6
  Multiplexer #(.Bits(16)) multiplexer_3 (.sel(jump), .in_0(multiplexer_2_out), .in_1(R_in), .out(R_out));

  assign rd = D[17:16];
  assign rs = D[21:20];

  // Notes on the sheet:
  //   D: Take 32-bits input
endmodule
