// Digital circuit execute.dig as structural Verilog
module execute (
  input  add,
  input  [15:0] value,
  input  [15:0] b,
  output [15:0] sum
);

  wire [15:0] add_1_s;

  Add #(.Bits(16)) add_1 (.a(value), .b(b), .c_i(1'b0), .s(add_1_s));  // open: c_o
  Multiplexer #(.Bits(16)) multiplexer_1 (.sel(add), .in_0(b), .in_1(add_1_s), .out(sum));
endmodule
