// Digital circuit fetch16.dig as structural Verilog
module fetch16 (
  input  mode,
  input  [31:0] D_stored,
  input  [31:0] D_bypass,
  input  C,
  input  [15:0] value,
  input  jump,
  output [3:0] pc,
  output [31:0] D_inst
);

  Multiplexer #(.Bits(32)) multiplexer_1 (.sel(mode), .in_0(D_stored), .in_1(D_bypass), .out(D_inst));
  CounterPreset #(.Bits(4)) u_PC (
    .en(1'b1), .C(C), .dir(1'b0), .in(value[3:0]), .ld(jump), .clr(1'b0), .out(pc));  // open: ovf

  // Notes on the sheet:
  //   mode: Take 32-bits input
  //   D_stored: Take 32-bits input
  //   D_bypass: Take 32-bits input
endmodule
