// Digital circuit hexdisplay.dig as structural Verilog
module hexdisplay (
  input  [31:0] V,
  output [3:0] D1,
  output P1,
  output P2,
  output P3,
  output P4,
  output P5,
  output P6,
  output P7,
  output P8,
  output [3:0] D2,
  output [3:0] D3,
  output [3:0] D4,
  output [3:0] D5,
  output [3:0] D6,
  output [3:0] D7,
  output [3:0] D8
);

  wire comparator_1_eq, comparator_2_eq, comparator_3_eq, comparator_4_eq, comparator_5_eq, comparator_6_eq,
       comparator_7_eq, comparator_8_eq, not_1_out, not_2_out, not_3_out, not_4_out, not_5_out, not_6_out,
       not_7_out, not_8_out;

  not not_1 (not_1_out, comparator_1_eq);
  Comparator #(.Bits(4)) comparator_1 (.a(V[31:28]), .b(4'b0000), .eq(comparator_1_eq));  // open: gt, lt
  assign D1 = not_1_out ? V[31:28] : 4'bz;  // Driver driver_1
  not not_2 (not_2_out, comparator_2_eq);
  Comparator #(.Bits(4)) comparator_2 (.a(V[27:24]), .b(4'b0000), .eq(comparator_2_eq));  // open: gt, lt
  assign D2 = not_2_out ? V[27:24] : 4'bz;  // Driver driver_2
  not not_3 (not_3_out, comparator_3_eq);
  Comparator #(.Bits(4)) comparator_3 (.a(V[23:20]), .b(4'b0000), .eq(comparator_3_eq));  // open: gt, lt
  assign D3 = not_3_out ? V[23:20] : 4'bz;  // Driver driver_3
  not not_4 (not_4_out, comparator_4_eq);
  Comparator #(.Bits(4)) comparator_4 (.a(V[19:16]), .b(4'b0000), .eq(comparator_4_eq));  // open: gt, lt
  assign D4 = not_4_out ? V[19:16] : 4'bz;  // Driver driver_4
  not not_5 (not_5_out, comparator_5_eq);
  Comparator #(.Bits(4)) comparator_5 (.a(V[15:12]), .b(4'b0000), .eq(comparator_5_eq));  // open: gt, lt
  assign D5 = not_5_out ? V[15:12] : 4'bz;  // Driver driver_5
  not not_6 (not_6_out, comparator_6_eq);
  Comparator #(.Bits(4)) comparator_6 (.a(V[11:8]), .b(4'b0000), .eq(comparator_6_eq));  // open: gt, lt
  assign D6 = not_6_out ? V[11:8] : 4'bz;  // Driver driver_6
  not not_7 (not_7_out, comparator_7_eq);
  Comparator #(.Bits(4)) comparator_7 (.a(V[7:4]), .b(4'b0000), .eq(comparator_7_eq));  // open: gt, lt
  assign D7 = not_7_out ? V[7:4] : 4'bz;  // Driver driver_7
  not not_8 (not_8_out, comparator_8_eq);
  Comparator #(.Bits(4)) comparator_8 (.a(V[3:0]), .b(4'b0000), .eq(comparator_8_eq));  // open: gt, lt
  assign D8 = not_8_out ? V[3:0] : 4'bz;  // Driver driver_8

  assign P1 = 1'b0;
  assign P2 = 1'b0;
  assign P3 = 1'b0;
  assign P4 = 1'b0;
  assign P5 = 1'b0;
  assign P6 = 1'b0;
  assign P7 = 1'b0;
  assign P8 = 1'b0;
endmodule
