// Digital circuit reg.dig as structural Verilog
module \reg  (
  input  [31:0] D,
  input  C,
  input  en,
  output [31:0] Q
);

  wire [31:0] multiplexer_1_out;

  Multiplexer #(.Bits(32)) multiplexer_1 (.sel(en), .in_0(Q), .in_1(D), .out(multiplexer_1_out));
  D_FF #(.Bits(32)) d_ff_1 (.D(multiplexer_1_out), .C(C), .Q(Q));  // open: nQ
endmodule
